# Fritzing sketch Display Serial (saved by Fritzing 0.9.3b)
breadboards: 1

parts:
  U1 = LCD-16X2 [package=lcd-16x2]
  T1 = LM35 Temperature Sensor [package="TO92 [THT]"]
  U2 = POT [package=pot_mammoth]
  Componente1 = Real Time Clock Module - DS1307 RTC Breakout Board
  R1 = Resistor [tolerance=±5% resistance=220 package=THT]
  Componente2 = Arduino Uno (Rev3) - ICSP

nets:
  GND: U1.VSS, U1.R_W, U1.K, T1.GND, U2.E, Componente1.GND, Componente2.GND
  5V: U1.VDD, T1.+Vs, U2.S, Componente1.5V, R1.Pin_0, Componente2.5V
  N1: U1.VO, U2.A
  N2: U1.RS, Componente2.D12/MISO
  N3: U1.E, Componente2.D11_PWM/MOSI
  N4: U1.DB4, Componente2.D5_PWM
  N5: U1.DB5, Componente2.D4
  N6: U1.DB6, Componente2.D3_PWM
  N7: U1.DB7, Componente2.D2
  N8: U1.A, R1.Pin_1
  N9: T1.Vout, Componente2.A0
  N10: Componente1.SQW, Componente2.D6_PWM
  N11: Componente1.SCL, Componente2.D7
  N12: Componente1.SDA, Componente2.D8
